// Digital circuit Register.dig as structural Verilog
module Register (
  input  [4:0] Rw,
  input  [31:0] Din,
  input  we,
  input  C,
  input  [4:0] Ra,
  input  [4:0] Rb,
  input  [23:0] in_9,
  input  C_2,
  input  [31:0] in_11,
  input  in_13,
  output [31:0] Da,
  output [31:0] Db,
  output [31:0] out_12
);

  Register Program_Counter ();  // open: D, C, en, Q
  RegisterFile #(.AddrBits(5), .Bits(32)) Register_File (
    .Din(Din), .we(we), .Rw(Rw), .C(C), .Ra(Ra), .Rb(Rb), .Da(Da), .Db(Db));
  ROM Inst_Memory ();  // open: A, sel, D
  BlockRAMDualPort #(.AddrBits(24), .Bits(32)) blockramdualport_1 (
    .A(in_9), .Din(in_11), .str(in_13), .C(C_2), .D(out_12));
endmodule
