// Digital circuit alu.dig as structural Verilog
module alu (
  input  [31:0] B,
  input  [1:0] ALUControl,
  input  [31:0] A,
  output Cout,
  output [31:0] Result,
  output N,
  output Z,
  output C,
  output V
);

  wire not_2_out, xnor_1_out, xor_1_out;
  wire [31:0] Adder_s, and_1_out, multiplexer_1_out, not_1_out, or_1_out;

  assign not_1_out = ~B;  // Not not_1, 32 bits wide
  xnor xnor_1 (xnor_1_out, A[31], B[31], ALUControl[0]);
  Multiplexer #(.Bits(32)) multiplexer_1 (.sel(ALUControl[0]), .in_0(B), .in_1(not_1_out), .out(multiplexer_1_out));
  not not_2 (not_2_out, ALUControl[1]);
  Add #(.Bits(32)) Adder (.a(A), .b(multiplexer_1_out), .c_i(ALUControl[0]), .s(Adder_s), .c_o(Cout));
  assign and_1_out = B & A;  // And and_1, 32 bits wide
  assign or_1_out = B | A;  // Or or_1, 32 bits wide
  and and_2 (C, Cout, not_2_out);
  xor xor_1 (xor_1_out, Adder_s[31], A[31]);
  Multiplexer #(.Selector_Bits(2), .Bits(32)) multiplexer_2 (
    .sel(ALUControl), .in_0(Adder_s), .in_1(Adder_s), .in_2(and_1_out), .in_3(or_1_out),
    .out({N, Result[30:0]}));
  nor_32 nor_32_1 (.A({N, Result[30:0]}), .Y(Z));
  and and_3 (V, not_2_out, xor_1_out, xnor_1_out);

  assign Result[31] = N;
endmodule
