// Digital circuit nor_32.dig as structural Verilog
module nor_32 (
  input  [31:0] A,
  output Y
);

  wire or_4_9_y, or_4_10_y;
  wire [3:0] or_4_1_y, or_4_5_y;

  or_4 or_4_1 (.A(A[3:0]), .Y(or_4_1_y[0]));
  or_4 or_4_2 (.A(A[7:4]), .Y(or_4_1_y[1]));
  or_4 or_4_3 (.A(A[11:8]), .Y(or_4_1_y[2]));
  or_4 or_4_4 (.A(A[15:12]), .Y(or_4_1_y[3]));
  or_4 or_4_5 (.A(A[19:16]), .Y(or_4_5_y[0]));
  or_4 or_4_6 (.A(A[23:20]), .Y(or_4_5_y[1]));
  or_4 or_4_7 (.A(A[27:24]), .Y(or_4_5_y[2]));
  or_4 or_4_8 (.A(A[31:28]), .Y(or_4_5_y[3]));
  or_4 or_4_9 (.A(or_4_1_y), .Y(or_4_9_y));
  or_4 or_4_10 (.A(or_4_5_y), .Y(or_4_10_y));
  nor nor_1 (Y, or_4_9_y, or_4_10_y);
endmodule
